// Logisim project tp2 structure S2.circ as structural Verilog: 3 circuits, main circuit main
module main (
  input  E3,
  input  E2,
  input  E1,
  input  E0
);

  wire \décodeur_mux_1_a , \décodeur_mux_1_b , \décodeur_mux_1_c , \décodeur_mux_1_d , \décodeur_mux_1_e ,
       \décodeur_mux_1_f , \décodeur_mux_1_g ;

  _7_Segment_Display u_7_segment_display_1 (
    .g(\décodeur_mux_1_g ), .f(\décodeur_mux_1_f ), .a(\décodeur_mux_1_a ), .b(\décodeur_mux_1_b ),
    .e(\décodeur_mux_1_e ), .d(\décodeur_mux_1_d ), .c(\décodeur_mux_1_c ));  // open: dp
  \décodeur_mux  \décodeur_mux_1  (
    .a(\décodeur_mux_1_a ), .b(\décodeur_mux_1_b ), .c(\décodeur_mux_1_c ), .d(\décodeur_mux_1_d ),
    .e(\décodeur_mux_1_e ), .f(\décodeur_mux_1_f ), .g(\décodeur_mux_1_g ), .E3(E3), .E2(E2), .E1(E1), .E0(E0));

  // Notes on the sheet:
  //   Tp 1 - Transcodeur Aiken vers afficheur 7 segments
  //   affiche E dans le cas d'une entrée non prise en compte
endmodule

module \décodeur  (
  input  E3,
  input  E2,
  input  E1,
  input  E0,
  output a,
  output b,
  output c,
  output d,
  output e,
  output f,
  output g
);

  wire and_1_out, and_2_out, and_3_out, and_4_out, and_5_out, and_6_out, and_7_out, and_8_out, and_9_out,
       and_10_out, and_11_out, and_12_out, not_1_out, not_2_out, not_3_out, not_4_out;

  not not_1 (not_1_out, E3);
  not not_2 (not_2_out, E2);
  not not_3 (not_3_out, E1);
  not not_4 (not_4_out, E0);
  and and_1 (and_1_out, E2, E0);
  and and_2 (and_2_out, not_2_out, not_4_out);
  and and_3 (and_3_out, E0, not_3_out);
  and and_4 (and_4_out, E1, E2);
  or or_1 (c, E3, not_3_out, E0);
  and and_5 (and_5_out, not_4_out, not_2_out);
  and and_6 (and_6_out, E3, not_4_out);
  and and_7 (and_7_out, E1, not_2_out);
  and and_8 (and_8_out, not_2_out, not_4_out);
  and and_9 (and_9_out, E3, not_4_out);
  and and_10 (and_10_out, not_3_out, not_4_out);
  and and_11 (and_11_out, E3, E1);
  and and_12 (and_12_out, not_4_out, E2);
  or or_2 (a, and_1_out, and_2_out, E1);
  or or_3 (b, and_3_out, and_4_out, not_1_out);
  or or_4 (d, and_5_out, and_6_out, and_7_out);
  or or_5 (e, and_8_out, and_9_out);
  or or_6 (f, and_10_out, and_11_out);
  or or_7 (g, and_12_out, E1);
endmodule

module \décodeur_mux  (
  input  E3,
  input  E2,
  input  E1,
  input  E0,
  output a,
  output b,
  output c,
  output d,
  output e,
  output f,
  output g
);

  wire not_1_out;

  not not_1 (not_1_out, 1'b1);
  Multiplexer #(.select(4), .enable("false")) multiplexer_1 (
    .in0(1'b1), .in1(not_1_out), .in2(1'b1), .in3(1'b1), .in4(not_1_out), .in5(1'b1), .in6(1'b1), .in7(1'b1),
    .in8(1'b1), .in9(1'b1), .in10(1'b1), .in11(1'b1), .in12(not_1_out), .in13(1'b1), .in14(1'b1),
    .in15(1'b1), .out(a), .sel({E3, E2, E1, E0}));
  Multiplexer #(.select(4), .enable("false")) multiplexer_2 (
    .in0(1'b1), .in1(1'b1), .in2(1'b1), .in3(1'b1), .in4(1'b1), .in5(not_1_out), .in6(not_1_out),
    .in7(not_1_out), .in8(not_1_out), .in9(not_1_out), .in10(not_1_out), .in11(not_1_out), .in12(not_1_out),
    .in13(1'b1), .in14(1'b1), .in15(1'b1), .out(b), .sel({E3, E2, E1, E0}));
  Multiplexer #(.select(4), .enable("false")) multiplexer_3 (
    .in0(1'b1), .in1(1'b1), .in2(not_1_out), .in3(1'b1), .in4(1'b1), .in5(not_1_out), .in6(not_1_out),
    .in7(not_1_out), .in8(not_1_out), .in9(not_1_out), .in10(not_1_out), .in11(1'b1), .in12(1'b1),
    .in13(1'b1), .in14(1'b1), .in15(1'b1), .out(c), .sel({E3, E2, E1, E0}));
  Multiplexer #(.select(4), .enable("false")) multiplexer_4 (
    .in0(1'b1), .in1(not_1_out), .in2(1'b1), .in3(1'b1), .in4(not_1_out), .in5(1'b1), .in6(1'b1), .in7(1'b1),
    .in8(1'b1), .in9(1'b1), .in10(1'b1), .in11(1'b1), .in12(1'b1), .in13(not_1_out), .in14(1'b1),
    .in15(not_1_out), .out(d), .sel({E3, E2, E1, E0}));
  Multiplexer #(.select(4), .enable("false")) multiplexer_5 (
    .in0(1'b1), .in1(not_1_out), .in2(1'b1), .in3(not_1_out), .in4(not_1_out), .in5(1'b1), .in6(1'b1),
    .in7(1'b1), .in8(1'b1), .in9(1'b1), .in10(1'b1), .in11(not_1_out), .in12(1'b1), .in13(not_1_out),
    .in14(1'b1), .in15(not_1_out), .out(e), .sel({E3, E2, E1, E0}));
  Multiplexer #(.select(4), .enable("false")) multiplexer_6 (
    .in0(1'b1), .in1(not_1_out), .in2(not_1_out), .in3(not_1_out), .in4(1'b1), .in5(1'b1), .in6(1'b1),
    .in7(1'b1), .in8(1'b1), .in9(1'b1), .in10(1'b1), .in11(1'b1), .in12(1'b1), .in13(not_1_out), .in14(1'b1),
    .in15(1'b1), .out(f), .sel({E3, E2, E1, E0}));
  Multiplexer #(.select(4), .enable("false")) multiplexer_7 (
    .in0(not_1_out), .in1(not_1_out), .in2(1'b1), .in3(1'b1), .in4(1'b1), .in5(1'b1), .in6(1'b1), .in7(1'b1),
    .in8(1'b1), .in9(1'b1), .in10(1'b1), .in11(1'b1), .in12(1'b1), .in13(not_1_out), .in14(1'b1),
    .in15(1'b1), .out(g), .sel({E3, E2, E1, E0}));
endmodule
